# Fritzing sketch pedal (saved by Fritzing 0.9.3b)

parts:
  SparkFun_Pro_Micro1 = SparkFun Pro Micro [part_number=DEV-12640]
  U1 = SWITCH_SPDT [package=kps-1290]
  S1 = Momentary Switch [package=ksa_sealed_tac_switch]
  S2 = Momentary Switch [package=ksa_sealed_tac_switch]
  S3 = Momentary Switch [package=ksa_sealed_tac_switch]
  S4 = Momentary Switch [package=ksa_sealed_tac_switch]
  S5 = Momentary Switch [package=ksa_sealed_tac_switch]
  LED1 = LED - 5mm [color="Red (633nm)" package="5 mm [THT]"]  # not connected
  LED2 = LED - 5mm [color="Red (633nm)" package="5 mm [THT]"]  # not connected
  LED3 = LED - 5mm [color="Red (633nm)" package="5 mm [THT]"]  # not connected
  LED4 = LED - 5mm [color="Red (633nm)" package="5 mm [THT]"]  # not connected
  LED5 = LED - 5mm [color="Red (633nm)" package="5 mm [THT]"]  # not connected
  R1 = Resistor [tolerance=±5% resistance=220 package="0603 [SMD]"]
  R2 = Resistor [tolerance=±5% resistance=220 package="0603 [SMD]"]
  R3 = Resistor [tolerance=±5% resistance=220 package="0603 [SMD]"]
  R4 = Resistor [tolerance=±5% resistance=220 package="0603 [SMD]"]
  R5 = Resistor [tolerance=±5% resistance=220 package="0603 [SMD]"]

nets:
  N1: SparkFun_Pro_Micro1.A0, R1.Pin_1
  N2: SparkFun_Pro_Micro1.SCK, R2.Pin_1
  N3: SparkFun_Pro_Micro1.MISO, R3.Pin_1
  N4: SparkFun_Pro_Micro1.MOSI, R4.Pin_1
  N5: SparkFun_Pro_Micro1.D10, R5.Pin_1
  N6: SparkFun_Pro_Micro1.D9, S1.4
  N7: SparkFun_Pro_Micro1.D8, S2.4
  N8: SparkFun_Pro_Micro1.D7, S3.4
  N9: SparkFun_Pro_Micro1.D6, S5.4
  N10: SparkFun_Pro_Micro1.D5, S4.4
  N11: SparkFun_Pro_Micro1.RXI, U1.O
  N12: SparkFun_Pro_Micro1.TXO, U1.S

notes:
  Resistors
  10 KOhm 0.5W
  SparkFun Pro Micro
  16Mhz model

custom parts:
  SparkFun Pro Micro: This tiny little board does all of the neat-o Arduino tricks that you’re familiar with: 4 channels of 10-bit ADC, 5 PWM pins, 12 DIOs as well as hardware serial connections Rx and Tx. Running at 16MHz and 5V, this board will remind you a lot of your other favorite Arduino-compatible boards but this little guy can go just about anywhere. There is a voltage regulator on board so it can accept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
